# Fritzing sketch Schema_platine_meteo (saved by Fritzing 0.9.2b)
breadboards: 1

parts:
  Arduino1 = Arduino Uno (Rev3)
  Light_sensor_(solar_cell) = S1133 Si Photodiode [package="8mm Ceramic [THT]"]
  R1 = Resistor [tolerance=±5% resistance=100 package="2512 [SMD]"]
  R2 = Resistor [tolerance=±5% resistance=1k package="2512 [SMD]"]
  R3 = Resistor [tolerance=±5% resistance=10k package="2512 [SMD]"]  # not connected
  Temp_/_Hum_Ext_Sensor = DHT22 Humidity and Temperature Sensor
  Temp_/_Hum_Int_Sensor = DHT22 Humidity and Temperature Sensor
  Wind_sensor = SWITCH-MOMENTARY-2 [package=reed_switch_pth]
  R4 = Resistor [tolerance=±5% resistance=10k package="2512 [SMD]"]
  Pressure_Sensor_(I2C) = Adafruit BME280
  IR_Sensor_(I2C) = MLX90614 [package=to-39]
  Rain_sensor = Telecontrolli IBR273
  R5 = Resistor [tolerance=±5% resistance=100k package="2512 [SMD]"]
  Q6 = npn-Powertransistor [package="TO220 [THT]"]
  Alimentation_12V = BATTERY-2 [package=battery-aaa]

nets:
  N1: Arduino1.A0, R1.Pin_1
  N2: Arduino1.A1, Rain_sensor.1
  N3: Arduino1.A2, Rain_sensor.6
  N4: Arduino1.A3, Rain_sensor.3, R5.Pin_0
  N5: Arduino1.A4/SDA, IR_Sensor_(I2C).PWM_SDA
  N6: Arduino1.A5/SCL, IR_Sensor_(I2C).SCL_VZ
  N7: Arduino1.D11_PWM/MOSI, Q6.base
  N8: Arduino1.D2, Temp_/_Hum_Int_Sensor.DATA
  N9: Arduino1.D4, Temp_/_Hum_Ext_Sensor.DATA
  VDD: Arduino1.5V, Temp_/_Hum_Ext_Sensor.VDD, Temp_/_Hum_Int_Sensor.VDD, R4.Pin_1, Pressure_Sensor_(I2C).VIN, IR_Sensor_(I2C).VDD, R5.Pin_1
  GND: Arduino1.GND, Light_sensor_(solar_cell).cathode, Temp_/_Hum_Ext_Sensor.GND, Temp_/_Hum_Int_Sensor.GND, Wind_sensor.1, Pressure_Sensor_(I2C).GND, IR_Sensor_(I2C).VSS, Rain_sensor.4, Q6.emitter, Alimentation_12V.-1
  N10: Light_sensor_(solar_cell).anode, R2.Pin_0
  N11: Rain_sensor.2, Alimentation_12V.+1
  N12: Rain_sensor.5, Q6.collector

custom parts:
  Adafruit BME280: Bosch has stepped up their game with their new BME280 sensor, an environmental sensor with temperature, barometric pressure and humidity! This sensor is great for all sorts of weather/environmental sensing and can even be used in both I2C and SPI! This precision sensor from Bosch is the best low-cost sensing solution for measuring humidity with ±3% accuracy, barometric pressure with ±1 hPa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
  Telecontrolli IBR273: Telecontrolli rain sensor is made of thickfilm technology and it is made up of three parts: • Capacitive sensor • Heater generator • Temperature sensor
